// Digital circuit Adder using custom adder.dig as structural Verilog
module Adder_using_custom_adder (
  input  A0,
  input  B0,
  input  A1,
  input  B1,
  input  A2,
  input  B2,
  output C0,
  output C1,
  output C2,
  output Carry
);

  wire fulladder_1_cout, fulladder_2_cout;

  FullAdder fulladder_1 (.A(A0), .B(B0), .Cin(1'b0), .S(C0), .Cout(fulladder_1_cout));
  FullAdder fulladder_2 (.A(A1), .B(B1), .Cin(fulladder_1_cout), .S(C1), .Cout(fulladder_2_cout));
  FullAdder fulladder_3 (.A(A2), .B(B2), .Cin(fulladder_2_cout), .S(C2), .Cout(Carry));
endmodule
