// Digital circuit 2BIT EQUALS COMPARTOR.dig as structural Verilog
module _2BIT_EQUALS_COMPARTOR (
  input  A1,
  input  A0,
  input  B1,
  input  B0,
  output E
);

  wire xnor_1_out, xnor_2_out;

  xnor xnor_1 (xnor_1_out, A1, B1);
  xnor xnor_2 (xnor_2_out, B0, A0);
  and and_1 (E, xnor_1_out, xnor_2_out);
endmodule
