// Digital circuit 2Bit Greater than compartor.dig as structural Verilog
module _2Bit_Greater_than_compartor (
  input  A0,
  input  A1,
  input  B0,
  input  B1,
  output Y
);

  wire and_1_out, and_2_out, and_3_out, not_1_out, not_2_out;

  not not_1 (not_1_out, B0);
  not not_2 (not_2_out, B1);
  and and_1 (and_1_out, A0, not_1_out, not_2_out);
  and and_2 (and_2_out, A0, A1, not_1_out);
  and and_3 (and_3_out, A1, not_2_out);
  or or_1 (Y, and_1_out, and_2_out, and_3_out);
endmodule
