// Digital circuit 4BITADDER.dig as structural Verilog
module _4BITADDER (
  input  Cin,
  input  A0,
  input  B0,
  input  A1,
  input  B1,
  input  A2,
  input  B2,
  input  A3,
  input  B3,
  output C0,
  output C1,
  output C2,
  output C3,
  output Cout
);

  wire addercircuit_1_cout, addercircuit_2_cout, addercircuit_3_cout;

  AdderCircuit addercircuit_1 (.Cin(Cin), .A(A0), .B(B0), .Sum(C0), .Cout(addercircuit_1_cout));
  AdderCircuit addercircuit_2 (.Cin(addercircuit_1_cout), .A(A1), .B(B1), .Sum(C1), .Cout(addercircuit_2_cout));
  AdderCircuit addercircuit_3 (.Cin(addercircuit_2_cout), .A(A2), .B(B2), .Sum(C2), .Cout(addercircuit_3_cout));
  AdderCircuit addercircuit_4 (.Cin(addercircuit_3_cout), .A(A3), .B(B3), .Sum(C3), .Cout(Cout));
endmodule
