// Digital circuit 4bit subtractor.dig as structural Verilog
module _4bit_subtractor (
  input  in_5,
  input  in_6,
  input  in_7,
  input  in_8,
  input  in_9,
  input  in_10,
  input  in_11,
  input  in_12,
  output out_1,
  output out_2,
  output out_3,
  output out_4
);

  wire xor_1_out, xor_2_out, xor_3_out, xor_4_out;

  // XOr xor_1 has open pins: In_1=open, In_2=open, out=xor_1_out
  // XOr xor_2 has open pins: In_1=open, In_2=open, out=xor_2_out
  // XOr xor_3 has open pins: In_1=open, In_2=open, out=xor_3_out
  // XOr xor_4 has open pins: In_1=open, In_2=open, out=xor_4_out
  _4BITADDER _4bitadder_1 (
    .B0(xor_1_out), .B1(xor_2_out), .B2(xor_3_out), .B3(xor_4_out), .C0(out_1), .C1(out_2), .C2(out_3),
    .C3(out_4));  // open: Cin, A0, A1, A2, A3, Cout
endmodule
