// Digital circuit Banda_W_2020010593 Bounus With single gate.dig as structural Verilog
module Banda_W_2020010593_Bounus_With_single_gate (
  input  A1,
  input  A0,
  input  B1,
  input  B0,
  output L,
  output E,
  output G
);

  wire nand_1_out, nand_2_out, nand_3_out, nand_4_out, nand_5_out, nand_6_out, nand_7_out, nand_8_out,
       nand_9_out, nand_10_out, not_1_out, not_2_out, not_3_out, not_4_out;

  not not_1 (not_1_out, A1);
  not not_2 (not_2_out, A0);
  not not_3 (not_3_out, B1);
  not not_4 (not_4_out, B0);
  nand nand_1 (nand_1_out, not_2_out, not_1_out, B0);
  nand nand_2 (nand_2_out, not_2_out, B0, B1);
  nand nand_3 (nand_3_out, not_1_out, B1);
  nand nand_4 (nand_4_out, not_2_out, not_1_out, not_4_out, not_3_out);
  nand nand_5 (nand_5_out, A0, not_1_out, B0, not_3_out);
  nand nand_6 (nand_6_out, not_2_out, A1, not_4_out, B1);
  nand nand_7 (nand_7_out, A0, A1, B0, B1);
  nand nand_8 (nand_8_out, A0, not_4_out, not_3_out);
  nand nand_9 (nand_9_out, A0, A1, not_4_out);
  nand nand_10 (nand_10_out, A1, not_3_out);
  nand nand_11 (L, nand_1_out, nand_2_out, nand_3_out);
  nand nand_12 (E, nand_4_out, nand_5_out, nand_6_out, nand_7_out);
  nand nand_13 (G, nand_8_out, nand_9_out, nand_10_out);
endmodule
