// Digital circuit ClassExercise.dig as structural Verilog
module ClassExercise (
  input  x,
  input  y,
  input  z,
  output q
);

  wire nor_1_out, nor_2_out, nor_3_out;

  nor nor_1 (nor_1_out, x, y);
  nor nor_2 (nor_2_out, x, z);
  nor nor_3 (nor_3_out, y, z);
  or or_1 (q, nor_1_out, nor_2_out, nor_3_out);
endmodule
