# Fritzing sketch GreenHouseModule (saved by Fritzing 0.9.3b)
breadboards: 1

parts:
  MH-ET_LIVE_ESP32_DEVKIT1 = MH-ET LIVE ESP32 DEVKIT 38 pins
  OLED1 = OLED 128x64 I2C Monochrome Display
  Part1 = MicroSD Card Module  # not connected

nets:
  3V3: MH-ET_LIVE_ESP32_DEVKIT1.3V3, OLED1.VDD
  N1: MH-ET_LIVE_ESP32_DEVKIT1.IO22, OLED1.SCK
  N2: MH-ET_LIVE_ESP32_DEVKIT1.IO21, OLED1.SDA
  N3: MH-ET_LIVE_ESP32_DEVKIT1.GND#70, OLED1.GND

custom parts:
  MH-ET LIVE ESP32 DEVKIT 38 pins: http://mh.nodebb.com/topic/2/mh-et-live-esp32-devkit
