# Fritzing sketch Multip0lexer pcb (saved by Fritzing 0.9.3b)
breadboards: 1

parts:
  S1 = Pushbutton [package="[THT]"]
  S2 = Pushbutton [package="[THT]"]
  S3 = Pushbutton [package="[THT]"]
  S4 = Pushbutton [package="[THT]"]
  S5 = Pushbutton [package="[THT]"]
  S6 = Pushbutton [package="[THT]"]
  S7 = Pushbutton [package="[THT]"]
  S8 = Pushbutton [package="[THT]"]
  S9 = Pushbutton [package="[THT]"]
  S10 = Pushbutton [package="[THT]"]
  S11 = Pushbutton [package="[THT]"]
  S12 = Pushbutton [package="[THT]"]
  S13 = Pushbutton [package="[THT]"]
  S14 = Pushbutton [package="[THT]"]
  S15 = Pushbutton [package="[THT]"]
  S16 = Pushbutton [package="[THT]"]
  S17 = Pushbutton [package="[THT]"]
  S18 = Pushbutton [package="[THT]"]
  S19 = Pushbutton [package="[THT]"]
  S20 = Pushbutton [package="[THT]"]
  S21 = Pushbutton [package="[THT]"]
  S22 = Pushbutton [package="[THT]"]
  S23 = Pushbutton [package="[THT]"]
  S24 = Pushbutton [package="[THT]"]
  S25 = Pushbutton [package="[THT]"]
  S26 = Pushbutton [package="[THT]"]
  S27 = Pushbutton [package="[THT]"]
  S28 = Pushbutton [package="[THT]"]
  S29 = Pushbutton [package="[THT]"]
  S30 = Pushbutton [package="[THT]"]
  S31 = Pushbutton [package="[THT]"]
  S32 = Pushbutton [package="[THT]"]
  S33 = Pushbutton [package="[THT]"]
  S34 = Pushbutton [package="[THT]"]
  S35 = Pushbutton [package="[THT]"]
  S36 = Pushbutton [package="[THT]"]
  S37 = Pushbutton [package="[THT]"]
  S38 = Pushbutton [package="[THT]"]
  S39 = Pushbutton [package="[THT]"]
  S40 = Pushbutton [package="[THT]"]
  S41 = Pushbutton [package="[THT]"]
  S42 = Pushbutton [package="[THT]"]
  S43 = Pushbutton [package="[THT]"]
  S44 = Pushbutton [package="[THT]"]
  S45 = Pushbutton [package="[THT]"]
  S46 = Pushbutton [package="[THT]"]
  S47 = Pushbutton [package="[THT]"]
  S48 = Pushbutton [package="[THT]"]
  S49 = Pushbutton [package="[THT]"]
  S50 = Pushbutton [package="[THT]"]
  S51 = Pushbutton [package="[THT]"]
  S52 = Pushbutton [package="[THT]"]
  S53 = Pushbutton [package="[THT]"]
  S54 = Pushbutton [package="[THT]"]
  S55 = Pushbutton [package="[THT]"]
  S56 = Pushbutton [package="[THT]"]
  S57 = Pushbutton [package="[THT]"]
  S58 = Pushbutton [package="[THT]"]
  S59 = Pushbutton [package="[THT]"]
  S60 = Pushbutton [package="[THT]"]
  S61 = Pushbutton [package="[THT]"]
  S62 = Pushbutton [package="[THT]"]
  S63 = Pushbutton [package="[THT]"]
  S64 = Pushbutton [package="[THT]"]
  U1 = 74HC595 [package="DIP16 [THT]"]

nets:
  N1: S1.Pin_1, S1.Pin_2, S2.Pin_1, S2.Pin_2, S3.Pin_1, S3.Pin_2, S4.Pin_1, S4.Pin_2, S5.Pin_1, S5.Pin_2, S6.Pin_1, S6.Pin_2, S7.Pin_1, S7.Pin_2, S8.Pin_1, S8.Pin_2, U1.Q0
  N2: S1.Pin_3, S10.Pin_3, S10.Pin_4, S18.Pin_3, S18.Pin_4, S19.Pin_3, S19.Pin_4, S34.Pin_3, S34.Pin_4, S38.Pin_3, S38.Pin_4, S39.Pin_3, S39.Pin_4, S40.Pin_4
  N3: S2.Pin_3, S11.Pin_3, S11.Pin_4, S31.Pin_3, S31.Pin_4, S32.Pin_3, S32.Pin_4, S42.Pin_3, S42.Pin_4, S48.Pin_4, S59.Pin_3, S59.Pin_4, S63.Pin_3, S63.Pin_4
  N4: S3.Pin_3, S13.Pin_3, S13.Pin_4, S21.Pin_3, S21.Pin_4, S24.Pin_3, S24.Pin_4, S41.Pin_3, S41.Pin_4, S49.Pin_3, S49.Pin_4, S54.Pin_4, S60.Pin_3, S60.Pin_4
  N5: S4.Pin_3, S16.Pin_3, S16.Pin_4, S23.Pin_3, S23.Pin_4, S30.Pin_3, S30.Pin_4, S44.Pin_3, S44.Pin_4, S51.Pin_3, S51.Pin_4, S61.Pin_4, S62.Pin_3, S62.Pin_4
  N6: S5.Pin_3, S9.Pin_3, S9.Pin_4, S17.Pin_3, S17.Pin_4, S20.Pin_3, S20.Pin_4, S33.Pin_3, S33.Pin_4, S35.Pin_3, S35.Pin_4, S36.Pin_3, S36.Pin_4, S37.Pin_3, S37.Pin_4
  N7: S6.Pin_3, S12.Pin_3, S12.Pin_4, S25.Pin_3, S25.Pin_4, S26.Pin_3, S26.Pin_4, S46.Pin_4, S53.Pin_3, S53.Pin_4, S55.Pin_3, S55.Pin_4, S64.Pin_3, S64.Pin_4
  N8: S7.Pin_3, S15.Pin_3, S15.Pin_4, S28.Pin_3, S28.Pin_4, S29.Pin_3, S29.Pin_4, S45.Pin_3, S45.Pin_4, S47.Pin_3, S47.Pin_4, S50.Pin_3, S50.Pin_4, S57.Pin_4
  N9: S8.Pin_3, S14.Pin_3, S14.Pin_4, S22.Pin_3, S22.Pin_4, S27.Pin_3, S27.Pin_4, S43.Pin_4, S52.Pin_3, S52.Pin_4, S56.Pin_3, S56.Pin_4, S58.Pin_3, S58.Pin_4
  N10: S9.Pin_1, S9.Pin_2, S10.Pin_1, S10.Pin_2, S11.Pin_1, S11.Pin_2, S12.Pin_1, S12.Pin_2, S13.Pin_1, S13.Pin_2, S14.Pin_1, S14.Pin_2, S15.Pin_1, S15.Pin_2, S16.Pin_1, S16.Pin_2, U1.Q1
  N11: S17.Pin_1, S17.Pin_2, S18.Pin_1, S18.Pin_2, S21.Pin_1, S21.Pin_2, S23.Pin_1, S23.Pin_2, S26.Pin_1, S26.Pin_2, S27.Pin_1, S27.Pin_2, S28.Pin_1, S28.Pin_2, S31.Pin_1, S31.Pin_2, U1.Q2
  N12: S19.Pin_1, S19.Pin_2, S20.Pin_1, S20.Pin_2, S22.Pin_1, S22.Pin_2, S24.Pin_1, S24.Pin_2, S25.Pin_1, S25.Pin_2, S29.Pin_1, S29.Pin_2, S30.Pin_1, S30.Pin_2, S32.Pin_1, S32.Pin_2, U1.Q3
  N13: S33.Pin_1, S33.Pin_2, S39.Pin_1, S39.Pin_2, S41.Pin_1, S41.Pin_2, S45.Pin_1, S45.Pin_2, S51.Pin_1, S51.Pin_2, S55.Pin_1, S55.Pin_2, S56.Pin_1, S56.Pin_2, S63.Pin_1, S63.Pin_2, U1.Q4
  N14: S34.Pin_1, S34.Pin_2, S35.Pin_1, S35.Pin_2, S44.Pin_1, S44.Pin_2, S49.Pin_1, S49.Pin_2, S50.Pin_1, S50.Pin_2, S53.Pin_1, S53.Pin_2, S58.Pin_1, S58.Pin_2, S59.Pin_1, S59.Pin_2, U1.Q5
  N15: S36.Pin_1, S36.Pin_2, S40.Pin_1, S40.Pin_2, S43.Pin_1, S43.Pin_2, S46.Pin_1, S46.Pin_2, S48.Pin_1, S48.Pin_2, S54.Pin_1, S54.Pin_2, S57.Pin_1, S57.Pin_2, S61.Pin_1, S61.Pin_2, U1.Q7
  N16: S37.Pin_1, S37.Pin_2, S38.Pin_1, S38.Pin_2, S42.Pin_1, S42.Pin_2, S47.Pin_1, S47.Pin_2, S52.Pin_1, S52.Pin_2, S60.Pin_1, S60.Pin_2, S62.Pin_1, S62.Pin_2, S64.Pin_1, S64.Pin_2, U1.Q6
