# Fritzing sketch MwizaWaterSensorV1 (saved by Fritzing 0.9.3b)
breadboards: 1

parts:
  V1 = DC Power [voltage=5]
  Q1 = NPN-Transistor [package="TO92 [THT]"]
  Q2 = NPN-Transistor [package="TO92 [THT]"]
  LED1 = LED - 5mm [color="Red (633nm)" package="5 mm [THT]"]
  R1 = Resistor [tolerance=±5% resistance=220 package=THT]
  J1 = female pin header, 2 pins [form="♀ (female)"]

nets:
  N1: V1.V+, Q1.C, Q2.C, J1.pin2
  N2: V1.V-, LED1.cathode
  N3: Q1.E, Q2.B
  N4: Q1.B, J1.pin1
  N5: Q2.E, R1.Pin_1
  N6: LED1.anode, R1.Pin_0

notes:
  Mwiza's Final Year Project
