// Digital circuit JK with D.dig as structural Verilog
module JK_with_D (
  input  a,
  input  clk,
  input  b,
  output out_4,
  output out_5
);

  wire and_1_out, and_2_out, and_3_out, d_ff_1_nq, d_ff_1_q, or_1_out, or_2_out;

  and and_1 (and_1_out, out_5, a);
  and and_2 (and_2_out, ~b, out_4, d_ff_1_q);  // And
  or or_1 (or_1_out, and_1_out, and_2_out);
  D_FF d_ff_1 (.D(or_1_out), .C(clk), .Q(d_ff_1_q), .nQ(d_ff_1_nq));
  and and_3 (and_3_out, ~d_ff_1_nq, out_4);  // And
  or or_2 (or_2_out, d_ff_1_q, and_3_out);
  D_FF d_ff_2 (.D(or_2_out), .C(~clk), .Q(out_4), .nQ(out_5));
endmodule
