// Digital circuit My CPU.dig as structural Verilog
module My_CPU (
  input  clk,
  input  Program,
  input  D0,
  input  D1,
  input  D2,
  input  D3,
  input  D4,
  input  D5,
  input  D6,
  input  D7,
  input  A3,
  input  A2,
  input  A1,
  input  A0,
  input  Reg_A_Reset,
  input  Reg_B_Reset,
  input  in_28,
  input  in_29,
  input  in_30,
  input  in_47,
  input  in_48,
  input  in_49,
  input  in_50,
  input  in_51,
  input  in_52,
  input  in_53,
  output out_2,
  output D7_2,
  output D6_2,
  output D5_2,
  output D4_2,
  output D3_2,
  output D2_2,
  output D1_2,
  output D0_2,
  output out_26,
  output out_27,
  output out_31,
  output out_32,
  output out_33,
  output out_34,
  output out_35,
  output out_36,
  output out_37,
  output out_38,
  output out_39,
  output out_40,
  output out_41,
  output out_42,
  output out_43,
  output out_44,
  output out_45,
  output out_46
);

  wire _7483real_1_pin4, _7483real_1_pin7, _7483real_1_pin11, _7483real_1_pin14, _7483real_1_pin16,
       _7483real_2_pin4, _7483real_2_pin7, _7483real_2_pin11, _7483real_2_pin16, _74162_2_pin11,
       _74162_2_pin12, _74162_2_pin13, _74162_2_pin14, _74173_1_pin11, _74173_1_pin12, _74173_1_pin13,
       _74173_1_pin14, _74189_1_pin5, _74189_1_pin7, _74189_1_pin9, _74189_1_pin11, _74189_2_pin5,
       _74189_2_pin7, _74189_2_pin9, _74189_2_pin11, _74245_4_pin11, _74245_4_pin12, _74245_4_pin13,
       _74245_4_pin14, _74245_4_pin15, _74245_4_pin16, _74245_4_pin17, _74245_4_pin18, _74245_5_pin11,
       _74245_5_pin12, _74245_5_pin13, _74245_5_pin14, _74245_5_pin15, _74245_5_pin16, _74245_5_pin17,
       _74245_5_pin18, _74245_6_pin11, _74245_6_pin12, _74245_6_pin13, _74245_6_pin14, _74245_6_pin15,
       _74245_6_pin16, _74245_6_pin17, _74245_6_pin18, and_1_out, driver_1_out, driver_2_out, driver_3_out,
       driver_4_out, driverinvsel_1_out, driverinvsel_2_out, driverinvsel_3_out, driverinvsel_4_out,
       driverinvsel_5_out, driverinvsel_6_out, driverinvsel_7_out, driverinvsel_8_out, driverinvsel_9_out,
       driverinvsel_10_out, driverinvsel_11_out, driverinvsel_12_out, not_1_out, not_2_out, not_3_out,
       not_4_out, not_5_out, not_6_out, not_7_out, not_8_out, not_9_out, or_1_out;
  wire [7:0] _74173_3_pin3;

  and and_1 (and_1_out, in_52, clk);
  not not_1 (not_1_out, and_1_out);
  _74162 _74162_1 (
    .pin1(out_33), .pin2(not_1_out), .pin3(1'b1), .pin4(1'b1), .pin5(1'b1), .pin6(1'b1), .pin7(out_34),
    .pin8(1'b0), .pin9(1'b1), .pin10(1'b1), .pin11(_74173_3_pin3[3]), .pin12(_74173_3_pin3[2]),
    .pin13(_74173_3_pin3[1]), .pin14(_74173_3_pin3[0]), .pin15(out_27), .pin16(1'b1));
  _74162 _74162_2 (
    .pin1(out_46), .pin2(clk), .pin3(1'b1), .pin4(1'b1), .pin5(1'b1), .pin6(1'b1), .pin7(out_31),
    .pin8(1'b0), .pin9(1'b1), .pin10(1'b1), .pin11(_74162_2_pin11), .pin12(_74162_2_pin12),
    .pin13(_74162_2_pin13), .pin14(_74162_2_pin14), .pin15(out_2), .pin16(1'b1));
  assign driverinvsel_1_out = ~Program ? A0 : 1'bz;  // DriverInvSel driverinvsel_1
  assign driverinvsel_2_out = ~Program ? A1 : 1'bz;  // DriverInvSel driverinvsel_2
  assign driverinvsel_3_out = ~Program ? A2 : 1'bz;  // DriverInvSel driverinvsel_3
  assign driverinvsel_4_out = ~Program ? A3 : 1'bz;  // DriverInvSel driverinvsel_4
  assign driver_1_out = out_37 ? driverinvsel_1_out : 1'bz;  // Driver driver_1
  assign driver_2_out = out_37 ? driverinvsel_2_out : 1'bz;  // Driver driver_2
  assign driver_3_out = out_37 ? driverinvsel_3_out : 1'bz;  // Driver driver_3
  assign driver_4_out = out_37 ? driverinvsel_4_out : 1'bz;  // Driver driver_4
  or or_1 (or_1_out, in_53, out_32);
  assign driverinvsel_5_out = ~Program ? D0 : 1'bz;  // DriverInvSel driverinvsel_5
  assign driverinvsel_6_out = ~Program ? D1 : 1'bz;  // DriverInvSel driverinvsel_6
  assign driverinvsel_7_out = ~Program ? D2 : 1'bz;  // DriverInvSel driverinvsel_7
  assign driverinvsel_8_out = ~Program ? D3 : 1'bz;  // DriverInvSel driverinvsel_8
  assign driverinvsel_9_out = ~Program ? D4 : 1'bz;  // DriverInvSel driverinvsel_9
  assign driverinvsel_10_out = ~Program ? D5 : 1'bz;  // DriverInvSel driverinvsel_10
  assign driverinvsel_11_out = ~Program ? D6 : 1'bz;  // DriverInvSel driverinvsel_11
  assign driverinvsel_12_out = ~Program ? D7 : 1'bz;  // DriverInvSel driverinvsel_12
  _74173 _74173_1 (
    .pin1(1'b0), .pin2(1'b0), .pin3(driver_1_out), .pin4(driver_2_out), .pin5(driver_3_out),
    .pin6(driver_4_out), .pin7(and_1_out), .pin8(1'b0), .pin9(out_37), .pin10(out_37),
    .pin11(_74173_1_pin11), .pin12(_74173_1_pin12), .pin13(_74173_1_pin13), .pin14(_74173_1_pin14),
    .pin15(out_37), .pin16(1'b1));
  _74189 _74189_1 (
    .pin1(driver_1_out), .pin2(1'b0), .pin3(or_1_out), .pin4(driverinvsel_5_out), .pin5(_74189_1_pin5),
    .pin6(driverinvsel_6_out), .pin7(_74189_1_pin7), .pin8(1'b0), .pin9(_74189_1_pin9),
    .pin10(driverinvsel_7_out), .pin11(_74189_1_pin11), .pin12(driverinvsel_8_out), .pin13(driver_4_out),
    .pin14(driver_3_out), .pin15(driver_2_out), .pin16(1'b1));
  _74189 _74189_2 (
    .pin1(driver_1_out), .pin2(1'b0), .pin3(or_1_out), .pin4(driverinvsel_9_out), .pin5(_74189_2_pin5),
    .pin6(driverinvsel_10_out), .pin7(_74189_2_pin7), .pin8(1'b0), .pin9(_74189_2_pin9),
    .pin10(driverinvsel_11_out), .pin11(_74189_2_pin11), .pin12(driverinvsel_12_out), .pin13(driver_4_out),
    .pin14(driver_3_out), .pin15(driver_2_out), .pin16(1'b1));
  not not_2 (not_2_out, _74189_1_pin11);
  not not_3 (not_3_out, _74189_1_pin7);
  not not_4 (not_4_out, _74189_1_pin9);
  not not_5 (not_5_out, _74189_2_pin11);
  not not_6 (not_6_out, _74189_2_pin9);
  not not_7 (not_7_out, _74189_1_pin5);
  not not_8 (not_8_out, _74189_2_pin7);
  not not_9 (not_9_out, _74189_2_pin5);
  _74245 _74245_1 (
    .pin1(1'b1), .pin2(_74162_2_pin14), .pin3(_74162_2_pin13), .pin4(_74162_2_pin12), .pin5(_74162_2_pin11),
    .pin6(1'b0), .pin7(1'b0), .pin8(1'b0), .pin9(1'b0), .pin10(1'b0), .pin11(in_51), .pin12(in_50),
    .pin13(in_48), .pin14(in_49), .pin15(D3_2), .pin16(D2_2), .pin17(D1_2), .pin18(D0_2), .pin19(out_45),
    .pin20(1'b1));
  _74245 _74245_2 (
    .pin1(1'b0), .pin2(driverinvsel_5_out), .pin3(driverinvsel_6_out), .pin4(driverinvsel_7_out),
    .pin5(driverinvsel_8_out), .pin6(driverinvsel_9_out), .pin7(driverinvsel_10_out),
    .pin8(driverinvsel_11_out), .pin9(driverinvsel_12_out), .pin10(1'b0), .pin11(D7_2), .pin12(D6_2),
    .pin13(D5_2), .pin14(D4_2), .pin15(D3_2), .pin16(D2_2), .pin17(D1_2), .pin18(D0_2), .pin19(out_35),
    .pin20(1'b1));
  _74245 _74245_3 (
    .pin1(1'b1), .pin2(not_7_out), .pin3(not_3_out), .pin4(not_4_out), .pin5(not_2_out), .pin6(not_9_out),
    .pin7(not_8_out), .pin8(not_6_out), .pin9(not_5_out), .pin10(1'b0), .pin11(D7_2), .pin12(D6_2),
    .pin13(D5_2), .pin14(D4_2), .pin15(D3_2), .pin16(D2_2), .pin17(D1_2), .pin18(D0_2), .pin19(out_36),
    .pin20(1'b1));
  _74173 _74173_2 (
    .pin1(1'b0), .pin2(1'b0), .pin3(_74173_1_pin14), .pin4(_74173_1_pin13), .pin5(_74173_1_pin12),
    .pin6(_74173_1_pin11), .pin7(and_1_out), .pin8(1'b0), .pin9(out_38), .pin10(out_38), .pin11(D3_2),
    .pin12(D2_2), .pin13(D1_2), .pin14(D0_2), .pin15(in_47), .pin16(1'b1));
  _74173 _74173_3 (
    .pin1(1'b0), .pin2(1'b0), .pin3(_74173_3_pin3[4]), .pin4(_74173_3_pin3[5]), .pin5(_74173_3_pin3[6]),
    .pin6(_74173_3_pin3[7]), .pin7(and_1_out), .pin8(1'b0), .pin9(out_38), .pin10(out_38), .pin11(D7_2),
    .pin12(D6_2), .pin13(D5_2), .pin14(D4_2), .pin15(in_47), .pin16(1'b1));
  EEPROM #(.AddrBits(8), .Bits(16)) eeprom_1 (
    .A(_74173_3_pin3), .CS(in_30), .WE(in_29), .OE(in_28),
    .D({out_46, out_45, out_44, out_43, out_42, out_41, out_40, out_39, out_38, out_37, out_36, out_35, out_34, out_33, out_32, out_31}));
  _74245 _74245_4 (
    .pin1(1'b0), .pin2(D0_2), .pin3(D1_2), .pin4(D2_2), .pin5(D3_2), .pin6(D4_2), .pin7(D5_2), .pin8(D6_2),
    .pin9(D7_2), .pin10(1'b0), .pin11(_74245_4_pin11), .pin12(_74245_4_pin12), .pin13(_74245_4_pin13),
    .pin14(_74245_4_pin14), .pin15(_74245_4_pin15), .pin16(_74245_4_pin16), .pin17(_74245_4_pin17),
    .pin18(_74245_4_pin18), .pin19(out_43), .pin20(1'b1));
  _74245 _74245_5 (
    .pin1(1'b0), .pin2(D0_2), .pin3(D1_2), .pin4(D2_2), .pin5(D3_2), .pin6(D4_2), .pin7(D5_2), .pin8(D6_2),
    .pin9(D7_2), .pin10(1'b0), .pin11(_74245_5_pin11), .pin12(_74245_5_pin12), .pin13(_74245_5_pin13),
    .pin14(_74245_5_pin14), .pin15(_74245_5_pin15), .pin16(_74245_5_pin16), .pin17(_74245_5_pin17),
    .pin18(_74245_5_pin18), .pin19(out_39), .pin20(1'b1));
  _7483Real _7483real_1 (
    .pin1(_74245_5_pin15), .pin2(_74245_4_pin16), .pin3(_74245_5_pin16), .pin4(_7483real_1_pin4),
    .pin5(1'b1), .pin6(_74245_4_pin17), .pin7(_7483real_1_pin7), .pin8(_74245_5_pin17),
    .pin9(_74245_4_pin18), .pin10(_74245_5_pin18), .pin11(_7483real_1_pin11), .pin12(1'b0), .pin13(out_44),
    .pin14(_7483real_1_pin14), .pin15(_74245_4_pin15), .pin16(_7483real_1_pin16));
  _7483Real _7483real_2 (
    .pin1(_74245_5_pin11), .pin2(_74245_4_pin12), .pin3(_74245_5_pin12), .pin4(_7483real_2_pin4),
    .pin5(1'b1), .pin6(_74245_4_pin13), .pin7(_7483real_2_pin7), .pin8(_74245_5_pin13),
    .pin9(_74245_4_pin14), .pin10(_74245_5_pin14), .pin11(_7483real_2_pin11), .pin12(1'b0),
    .pin13(_7483real_1_pin14), .pin14(out_26), .pin15(_74245_4_pin11), .pin16(_7483real_2_pin16));
  _74245 _74245_6 (
    .pin1(1'b0), .pin2(D0_2), .pin3(D1_2), .pin4(D2_2), .pin5(D3_2), .pin6(D4_2), .pin7(D5_2), .pin8(D6_2),
    .pin9(D7_2), .pin10(1'b0), .pin11(_74245_6_pin11), .pin12(_74245_6_pin12), .pin13(_74245_6_pin13),
    .pin14(_74245_6_pin14), .pin15(_74245_6_pin15), .pin16(_74245_6_pin16), .pin17(_74245_6_pin17),
    .pin18(_74245_6_pin18), .pin19(out_41), .pin20(1'b1));
  _7486 _7486_1 (
    .pin1(_74245_6_pin18), .pin2(out_44), .pin3(_7483real_1_pin11), .pin4(_74245_6_pin17), .pin5(out_44),
    .pin6(_7483real_1_pin7), .pin7(1'b0), .pin8(_7483real_1_pin4), .pin9(_74245_6_pin16), .pin10(out_44),
    .pin11(_7483real_1_pin16), .pin12(_74245_6_pin15), .pin13(out_44), .pin14(1'b1));
  _7486 _7486_2 (
    .pin1(_74245_6_pin14), .pin2(out_44), .pin3(_7483real_2_pin11), .pin4(_74245_6_pin13), .pin5(out_44),
    .pin6(_7483real_2_pin7), .pin7(1'b0), .pin8(_7483real_2_pin4), .pin9(_74245_6_pin12), .pin10(out_44),
    .pin11(_7483real_2_pin16), .pin12(_74245_6_pin11), .pin13(out_44), .pin14(1'b1));
  _74173 _74173_4 (
    .pin1(1'b0), .pin2(1'b0), .pin3(_74245_5_pin18), .pin4(_74245_5_pin17), .pin5(_74245_5_pin16),
    .pin6(_74245_5_pin15), .pin7(clk), .pin8(1'b0), .pin9(out_40), .pin10(out_40), .pin11(D3_2),
    .pin12(D2_2), .pin13(D1_2), .pin14(D0_2), .pin15(Reg_A_Reset), .pin16(1'b1));
  _74173 _74173_5 (
    .pin1(1'b0), .pin2(1'b0), .pin3(_74245_5_pin14), .pin4(_74245_5_pin13), .pin5(_74245_5_pin12),
    .pin6(_74245_5_pin11), .pin7(clk), .pin8(1'b0), .pin9(out_40), .pin10(out_40), .pin11(D7_2),
    .pin12(D6_2), .pin13(D5_2), .pin14(D4_2), .pin15(Reg_A_Reset), .pin16(1'b1));
  _74173 _74173_6 (
    .pin1(1'b0), .pin2(1'b0), .pin3(_74245_6_pin18), .pin4(_74245_6_pin17), .pin5(_74245_6_pin16),
    .pin6(_74245_6_pin15), .pin7(clk), .pin8(1'b0), .pin9(out_42), .pin10(out_42), .pin11(D3_2),
    .pin12(D2_2), .pin13(D1_2), .pin14(D0_2), .pin15(Reg_B_Reset), .pin16(1'b1));
  _74173 _74173_7 (
    .pin1(1'b0), .pin2(1'b0), .pin3(_74245_6_pin14), .pin4(_74245_6_pin13), .pin5(_74245_6_pin12),
    .pin6(_74245_6_pin11), .pin7(clk), .pin8(1'b0), .pin9(out_42), .pin10(out_42), .pin11(D7_2),
    .pin12(D6_2), .pin13(D5_2), .pin14(D4_2), .pin15(Reg_B_Reset), .pin16(1'b1));

  // Other names for the same wires on the sheet: EnableCount = out_31; RME = out_32; ClearInstCount = out_33;
  //   EnableIC = out_34; RAMIN = out_35; RAMOUT = out_36; MAROUT = out_37; LOADMAR = out_38; OUTA = out_39;
  //   LOADA = out_40; OUTB = out_41; LOADB = out_42; ALUOUT = out_43; SUB = out_44; COUNTER_OUT = out_45;
  //   COUNTER_RESET = out_46

  // Notes on the sheet:
  //   clk: Hz: 10
  //   Program: default 1
  //   in_28: default 1
  //   in_30: default 1
  //   Programmable Ram
  //   contents of eeprom_1 (hex, n*v repeats v):
  //   40c0,a0,40,4,5,6,7,8,9,a,b,c,d,e,f,10,a,16*0,a,16*0,8,16*0,8,15*0
  //   ,4d,49,16*0,a,16*0,ea,16*0,22
endmodule
