// Digital circuit MyCPU V2.dig as structural Verilog
module MyCPU_V2 (
  input  in_1,
  input  in_2,
  input  in_3,
  input  in_4,
  input  in_5,
  input  in_6,
  input  in_7,
  input  in_8,
  input  in_9,
  input  in_10,
  input  in_11,
  input  in_12,
  input  in_21,
  input  in_22,
  input  in_23,
  input  Enable_Counter,
  input  in_26,
  input  in_27,
  input  clk,
  input  in_29,
  input  Reg_A_Reset,
  input  Reg_B_Reset,
  input  in_33,
  input  in_34,
  input  in_35,
  input  in_36,
  input  in_37,
  input  in_38,
  input  in_39,
  input  in_40,
  input  in_41,
  input  in_42,
  input  in_43,
  input  ICR,
  input  in_46,
  input  in_47,
  input  in_48,
  input  in_49,
  input  in_66,
  input  in_67,
  input  in_68,
  output out_13,
  output out_14,
  output out_15,
  output out_16,
  output out_17,
  output out_18,
  output out_19,
  output out_20,
  output out_24,
  output out_32,
  output out_44,
  output out_50,
  output out_51,
  output out_52,
  output out_53,
  output out_54,
  output out_55,
  output out_56,
  output out_57,
  output out_58,
  output out_59,
  output out_60,
  output out_61,
  output out_62,
  output out_63,
  output out_64,
  output out_65,
  output out_69,
  output out_70,
  output out_71,
  output out_72,
  output out_73,
  output out_74,
  output out_75,
  output out_76,
  output out_77,
  output out_78,
  output out_79,
  output out_80,
  output out_81,
  output out_82,
  output out_83,
  output out_84
);

  wire _7483real_1_pin4, _7483real_1_pin7, _7483real_1_pin11, _7483real_1_pin14, _7483real_1_pin16,
       _7483real_2_pin4, _7483real_2_pin7, _7483real_2_pin11, _7483real_2_pin16, _74162_1_pin2,
       _74162_2_pin3, _74162_2_pin4, _74162_2_pin5, _74162_2_pin6, _74162_2_pin11, _74162_2_pin12,
       _74162_2_pin13, _74162_2_pin14, _74173_1_pin3, _74173_1_pin4, _74173_1_pin5, _74173_1_pin6,
       _74173_1_pin11, _74173_1_pin12, _74173_1_pin13, _74173_1_pin14, _74173_2_pin3, _74173_2_pin4,
       _74173_2_pin5, _74173_2_pin6, _74173_2_pin11, _74173_2_pin12, _74173_2_pin13, _74173_2_pin14,
       _74189_1_pin5, _74189_1_pin7, _74189_1_pin9, _74189_1_pin11, _74189_2_pin5, _74189_2_pin7,
       _74189_2_pin9, _74189_2_pin11, _74245_2_pin15, _74245_2_pin16, _74245_2_pin17, _74245_2_pin18,
       _74245_9_pin11, _74245_9_pin12, _74245_9_pin13, _74245_9_pin14, _74245_9_pin15, _74245_9_pin16,
       _74245_9_pin17, _74245_9_pin18, _74245_10_pin11, _74245_10_pin12, _74245_10_pin13, _74245_10_pin14,
       _74245_10_pin15, _74245_10_pin16, _74245_10_pin17, _74245_10_pin18, _74245_11_pin11, _74245_11_pin12,
       _74245_11_pin13, _74245_11_pin14, _74245_11_pin15, _74245_11_pin16, _74245_11_pin17, _74245_11_pin18,
       Clock, not_2_out, not_3_out, not_4_out, not_5_out, not_6_out, not_7_out, not_8_out, not_9_out,
       not_10_out, switch_1_b, switch_2_b, switch_3_b, switch_4_b, switch_5_b, switch_6_b, switch_7_b,
       switch_8_b, switch_9_b, switch_10_b, switch_11_b, switch_12_b;
  wire [7:0] _74162_1_pin14, eeprom_1_d;

  Switch #(.Closed("true")) switch_1 (.A(in_9), .B(switch_1_b));
  Switch #(.Closed("true")) switch_2 (.A(in_10), .B(switch_2_b));
  Switch #(.Closed("true")) switch_3 (.A(in_11), .B(switch_3_b));
  Switch #(.Closed("true")) switch_4 (.A(in_12), .B(switch_4_b));
  EEPROM #(.AddrBits(4), .Bits(8)) eeprom_1 (
    .A({in_12, in_11, in_10, in_9}), .CS(in_68), .WE(in_67), .OE(in_66), .D(eeprom_1_d));
  Switch #(.Closed("true")) switch_5 (.A(eeprom_1_d[0]), .B(switch_5_b));
  Switch #(.Closed("true")) switch_6 (.A(eeprom_1_d[1]), .B(switch_6_b));
  Switch #(.Closed("true")) switch_7 (.A(eeprom_1_d[2]), .B(switch_7_b));
  Switch #(.Closed("true")) switch_8 (.A(eeprom_1_d[3]), .B(switch_8_b));
  Switch #(.Closed("true")) switch_9 (.A(eeprom_1_d[4]), .B(switch_9_b));
  Switch #(.Closed("true")) switch_10 (.A(eeprom_1_d[5]), .B(switch_10_b));
  Switch #(.Closed("true")) switch_11 (.A(eeprom_1_d[6]), .B(switch_11_b));
  Switch #(.Closed("true")) switch_12 (.A(eeprom_1_d[7]), .B(switch_12_b));
  _74162 _74162_1 (
    .pin1(out_65), .pin2(_74162_1_pin2), .pin3(1'b1), .pin4(1'b1), .pin5(1'b1), .pin6(1'b1), .pin7(in_46),
    .pin8(1'b0), .pin9(1'b1), .pin10(1'b1), .pin11(_74162_1_pin14[3]), .pin12(_74162_1_pin14[2]),
    .pin13(_74162_1_pin14[1]), .pin14(_74162_1_pin14[0]), .pin15(out_44), .pin16(1'b1));
  not not_1 (_74162_1_pin2, Clock);
  not not_2 (not_2_out, out_64);
  _74189 _74189_1 (
    .pin1(switch_1_b), .pin2(1'b0), .pin3(in_23), .pin4(switch_5_b), .pin5(_74189_1_pin5), .pin6(switch_6_b),
    .pin7(_74189_1_pin7), .pin8(1'b0), .pin9(_74189_1_pin9), .pin10(switch_7_b), .pin11(_74189_1_pin11),
    .pin12(switch_8_b), .pin13(switch_4_b), .pin14(switch_3_b), .pin15(switch_2_b), .pin16(1'b1));
  _74189 _74189_2 (
    .pin1(switch_1_b), .pin2(1'b0), .pin3(in_23), .pin4(switch_9_b), .pin5(_74189_2_pin5),
    .pin6(switch_10_b), .pin7(_74189_2_pin7), .pin8(1'b0), .pin9(_74189_2_pin9), .pin10(switch_11_b),
    .pin11(_74189_2_pin11), .pin12(switch_12_b), .pin13(switch_4_b), .pin14(switch_3_b), .pin15(switch_2_b),
    .pin16(1'b1));
  _74173 _74173_1 (
    .pin1(1'b0), .pin2(1'b0), .pin3(_74173_1_pin3), .pin4(_74173_1_pin4), .pin5(_74173_1_pin5),
    .pin6(_74173_1_pin6), .pin7(Clock), .pin8(1'b0), .pin9(out_53), .pin10(out_53), .pin11(_74173_1_pin11),
    .pin12(_74173_1_pin12), .pin13(_74173_1_pin13), .pin14(_74173_1_pin14), .pin15(out_69), .pin16(1'b1));
  _74173 _74173_2 (
    .pin1(1'b0), .pin2(1'b0), .pin3(_74173_2_pin3), .pin4(_74173_2_pin4), .pin5(_74173_2_pin5),
    .pin6(_74173_2_pin6), .pin7(Clock), .pin8(1'b0), .pin9(out_53), .pin10(out_53), .pin11(_74173_2_pin11),
    .pin12(_74173_2_pin12), .pin13(_74173_2_pin13), .pin14(_74173_2_pin14), .pin15(out_69), .pin16(1'b1));
  _74245 _74245_1 (
    .pin1(1'b1), .pin2(_74173_2_pin3), .pin3(_74173_2_pin4), .pin4(_74173_2_pin5), .pin5(_74173_2_pin6),
    .pin10(1'b0), .pin15(_74162_1_pin14[7]), .pin16(_74162_1_pin14[6]), .pin17(_74162_1_pin14[5]),
    .pin18(_74162_1_pin14[4]), .pin19(out_70), .pin20(1'b1));  // open: pin6, pin7, pin8, pin9, pin11, pin12, pin13, pin14
  _74162 _74162_2 (
    .pin1(in_27), .pin2(Clock), .pin3(_74162_2_pin3), .pin4(_74162_2_pin4), .pin5(_74162_2_pin5),
    .pin6(_74162_2_pin6), .pin7(not_2_out), .pin8(1'b0), .pin9(out_63), .pin10(1'b1), .pin11(_74162_2_pin11),
    .pin12(_74162_2_pin12), .pin13(_74162_2_pin13), .pin14(_74162_2_pin14), .pin15(out_24), .pin16(1'b1));
  _74245 _74245_2 (
    .pin1(1'b0), .pin2(switch_1_b), .pin3(switch_2_b), .pin4(switch_3_b), .pin5(switch_4_b), .pin10(1'b0),
    .pin15(_74245_2_pin15), .pin16(_74245_2_pin16), .pin17(_74245_2_pin17), .pin18(_74245_2_pin18),
    .pin19(out_50), .pin20(1'b1));  // open: pin6, pin7, pin8, pin9, pin11, pin12, pin13, pin14
  PullDown pulldown_1 (.out(_74162_1_pin14[7]));
  PullDown pulldown_2 (.out(_74162_1_pin14[6]));
  PullDown pulldown_3 (.out(_74162_1_pin14[5]));
  PullDown pulldown_4 (.out(_74162_1_pin14[4]));
  not not_3 (not_3_out, _74189_1_pin5);
  not not_4 (not_4_out, _74189_1_pin7);
  not not_5 (not_5_out, _74189_1_pin9);
  not not_6 (not_6_out, _74189_1_pin11);
  not not_7 (not_7_out, _74189_2_pin5);
  not not_8 (not_8_out, _74189_2_pin7);
  not not_9 (not_9_out, _74189_2_pin9);
  not not_10 (not_10_out, _74189_2_pin11);
  _74173 _74173_3 (
    .pin1(1'b0), .pin2(1'b0), .pin3(_74245_2_pin18), .pin4(_74245_2_pin17), .pin5(_74245_2_pin16),
    .pin6(_74245_2_pin15), .pin7(Clock), .pin8(1'b0), .pin9(out_51), .pin10(out_51), .pin11(out_17),
    .pin12(out_18), .pin13(out_19), .pin14(out_20), .pin15(in_42), .pin16(1'b1));
  _74245 _74245_3 (
    .pin1(1'b0), .pin6(_74162_2_pin3), .pin7(_74162_2_pin4), .pin8(_74162_2_pin5), .pin9(_74162_2_pin6),
    .pin10(1'b0), .pin11(out_17), .pin12(out_18), .pin13(out_19), .pin14(out_20), .pin19(out_63), .pin20(1'b1));  // open: pin2, pin3, pin4, pin5, pin15, pin16, pin17, pin18
  _74245 _74245_4 (
    .pin1(1'b1), .pin6(_74162_2_pin14), .pin7(_74162_2_pin13), .pin8(_74162_2_pin12), .pin9(_74162_2_pin11),
    .pin10(1'b0), .pin11(out_17), .pin12(out_18), .pin13(out_19), .pin14(out_20), .pin19(out_62), .pin20(1'b1));  // open: pin2, pin3, pin4, pin5, pin15, pin16, pin17, pin18
  _74245 _74245_5 (
    .pin1(1'b0), .pin2(switch_5_b), .pin3(switch_6_b), .pin4(switch_7_b), .pin5(switch_8_b),
    .pin6(switch_9_b), .pin7(switch_10_b), .pin8(switch_11_b), .pin9(switch_12_b), .pin10(1'b0),
    .pin11(out_13), .pin12(out_14), .pin13(out_15), .pin14(out_16), .pin15(out_17), .pin16(out_18),
    .pin17(out_19), .pin18(out_20), .pin19(out_55), .pin20(1'b1));
  _74245 _74245_6 (
    .pin1(1'b1), .pin2(not_3_out), .pin3(not_4_out), .pin4(not_5_out), .pin5(not_6_out), .pin6(not_7_out),
    .pin7(not_8_out), .pin8(not_9_out), .pin9(not_10_out), .pin10(1'b0), .pin11(out_13), .pin12(out_14),
    .pin13(out_15), .pin14(out_16), .pin15(out_17), .pin16(out_18), .pin17(out_19), .pin18(out_20),
    .pin19(out_54), .pin20(1'b1));
  _74245 _74245_7 (
    .pin1(1'b0), .pin2(_74173_1_pin14), .pin3(_74173_1_pin13), .pin4(_74173_1_pin12), .pin5(_74173_1_pin11),
    .pin6(_74173_2_pin14), .pin7(_74173_2_pin13), .pin8(_74173_2_pin12), .pin9(_74173_2_pin11), .pin10(1'b0),
    .pin11(out_13), .pin12(out_14), .pin13(out_15), .pin14(out_16), .pin15(out_17), .pin16(out_18),
    .pin17(out_19), .pin18(out_20), .pin19(out_53), .pin20(1'b1));
  _74245 _74245_8 (
    .pin1(1'b1), .pin2(_74173_1_pin3), .pin3(_74173_1_pin4), .pin4(_74173_1_pin5), .pin5(_74173_1_pin6),
    .pin6(_74173_2_pin3), .pin7(_74173_2_pin4), .pin8(_74173_2_pin5), .pin9(_74173_2_pin6), .pin10(1'b0),
    .pin11(out_13), .pin12(out_14), .pin13(out_15), .pin14(out_16), .pin15(out_17), .pin16(out_18),
    .pin17(out_19), .pin18(out_20), .pin19(out_52), .pin20(1'b1));
  and and_1 (Clock, in_43, clk);
  EEPROM #(.AddrBits(8), .Bits(32)) eeprom_2 (
    .A(_74162_1_pin14), .CS(in_49), .WE(in_48), .OE(in_47),
    .D({out_84, out_83, out_82, out_81, out_80, out_79, out_78, out_77, out_76, out_75, out_74, out_73, out_72, out_71, out_70, out_69, out_65, out_64, out_63, out_62, out_61, out_60, out_59, out_58, out_57, out_56, out_55, out_54, out_53, out_52, out_51, out_50}));
  _74245 _74245_9 (
    .pin1(1'b0), .pin2(out_20), .pin3(out_19), .pin4(out_18), .pin5(out_17), .pin6(out_16), .pin7(out_15),
    .pin8(out_14), .pin9(out_13), .pin10(1'b0), .pin11(_74245_9_pin11), .pin12(_74245_9_pin12),
    .pin13(_74245_9_pin13), .pin14(_74245_9_pin14), .pin15(_74245_9_pin15), .pin16(_74245_9_pin16),
    .pin17(_74245_9_pin17), .pin18(_74245_9_pin18), .pin19(out_57), .pin20(1'b1));
  _74245 _74245_10 (
    .pin1(1'b0), .pin2(out_20), .pin3(out_19), .pin4(out_18), .pin5(out_17), .pin6(out_16), .pin7(out_15),
    .pin8(out_14), .pin9(out_13), .pin10(1'b0), .pin11(_74245_10_pin11), .pin12(_74245_10_pin12),
    .pin13(_74245_10_pin13), .pin14(_74245_10_pin14), .pin15(_74245_10_pin15), .pin16(_74245_10_pin16),
    .pin17(_74245_10_pin17), .pin18(_74245_10_pin18), .pin19(out_61), .pin20(1'b1));
  _7483Real _7483real_1 (
    .pin1(_74245_10_pin15), .pin2(_74245_9_pin16), .pin3(_74245_10_pin16), .pin4(_7483real_1_pin4),
    .pin5(1'b1), .pin6(_74245_9_pin17), .pin7(_7483real_1_pin7), .pin8(_74245_10_pin17),
    .pin9(_74245_9_pin18), .pin10(_74245_10_pin18), .pin11(_7483real_1_pin11), .pin12(1'b0), .pin13(out_56),
    .pin14(_7483real_1_pin14), .pin15(_74245_9_pin15), .pin16(_7483real_1_pin16));
  _7483Real _7483real_2 (
    .pin1(_74245_10_pin11), .pin2(_74245_9_pin12), .pin3(_74245_10_pin12), .pin4(_7483real_2_pin4),
    .pin5(1'b1), .pin6(_74245_9_pin13), .pin7(_7483real_2_pin7), .pin8(_74245_10_pin13),
    .pin9(_74245_9_pin14), .pin10(_74245_10_pin14), .pin11(_7483real_2_pin11), .pin12(1'b0),
    .pin13(_7483real_1_pin14), .pin14(out_32), .pin15(_74245_9_pin11), .pin16(_7483real_2_pin16));
  _74245 _74245_11 (
    .pin1(1'b0), .pin2(out_20), .pin3(out_19), .pin4(out_18), .pin5(out_17), .pin6(out_16), .pin7(out_15),
    .pin8(out_14), .pin9(out_13), .pin10(1'b0), .pin11(_74245_11_pin11), .pin12(_74245_11_pin12),
    .pin13(_74245_11_pin13), .pin14(_74245_11_pin14), .pin15(_74245_11_pin15), .pin16(_74245_11_pin16),
    .pin17(_74245_11_pin17), .pin18(_74245_11_pin18), .pin19(out_59), .pin20(1'b1));
  _7486 _7486_1 (
    .pin1(_74245_11_pin18), .pin2(out_56), .pin3(_7483real_1_pin11), .pin4(_74245_11_pin17), .pin5(out_56),
    .pin6(_7483real_1_pin7), .pin7(1'b0), .pin8(_7483real_1_pin4), .pin9(_74245_11_pin16), .pin10(out_56),
    .pin11(_7483real_1_pin16), .pin12(_74245_11_pin15), .pin13(out_56), .pin14(1'b1));
  _7486 _7486_2 (
    .pin1(_74245_11_pin14), .pin2(out_56), .pin3(_7483real_2_pin11), .pin4(_74245_11_pin13), .pin5(out_56),
    .pin6(_7483real_2_pin7), .pin7(1'b0), .pin8(_7483real_2_pin4), .pin9(_74245_11_pin12), .pin10(out_56),
    .pin11(_7483real_2_pin16), .pin12(_74245_11_pin11), .pin13(out_56), .pin14(1'b1));
  _74173 _74173_4 (
    .pin1(1'b0), .pin2(1'b0), .pin3(_74245_10_pin18), .pin4(_74245_10_pin17), .pin5(_74245_10_pin16),
    .pin6(_74245_10_pin15), .pin7(Clock), .pin8(1'b0), .pin9(out_60), .pin10(out_60), .pin11(out_17),
    .pin12(out_18), .pin13(out_19), .pin14(out_20), .pin15(Reg_A_Reset), .pin16(1'b1));
  _74173 _74173_5 (
    .pin1(1'b0), .pin2(1'b0), .pin3(_74245_10_pin14), .pin4(_74245_10_pin13), .pin5(_74245_10_pin12),
    .pin6(_74245_10_pin11), .pin7(Clock), .pin8(1'b0), .pin9(out_60), .pin10(out_60), .pin11(out_13),
    .pin12(out_14), .pin13(out_15), .pin14(out_16), .pin15(Reg_A_Reset), .pin16(1'b1));
  _74173 _74173_6 (
    .pin1(1'b0), .pin2(1'b0), .pin3(_74245_11_pin18), .pin4(_74245_11_pin17), .pin5(_74245_11_pin16),
    .pin6(_74245_11_pin15), .pin7(Clock), .pin8(1'b0), .pin9(out_58), .pin10(out_58), .pin11(out_17),
    .pin12(out_18), .pin13(out_19), .pin14(out_20), .pin15(Reg_B_Reset), .pin16(1'b1));
  _74173 _74173_7 (
    .pin1(1'b0), .pin2(1'b0), .pin3(_74245_11_pin14), .pin4(_74245_11_pin13), .pin5(_74245_11_pin12),
    .pin6(_74245_11_pin11), .pin7(Clock), .pin8(1'b0), .pin9(out_58), .pin10(out_58), .pin11(out_13),
    .pin12(out_14), .pin13(out_15), .pin14(out_16), .pin15(Reg_B_Reset), .pin16(1'b1));

  // Other names for the same wires on the sheet: MAROUT = out_50; MARIN = out_51; IROUT = out_52; IRIN = out_53;
  //   RAMOUT = out_54; RAMIN = out_55; SUB = out_56; ALUOUT = out_57; LDB = out_58; OUTB = out_59; LDA = out_60;
  //   OUTA = out_61; COUNTOUT = out_62; COUNTIN = out_63; COUNTENABLE = out_64; ICENABLE = out_65; IRRESET = out_69;
  //   CUIN = out_70

  // Notes on the sheet:
  //   in_21: default 1
  //   in_22: default 1
  //   in_26: default 1
  //   in_27: default 1
  //   in_29: default 1
  //   in_39: default 1
  //   in_40: default 1
  //   in_41: default 1
  //   ICR: default 1
  //   in_46: default 1
  //   in_47: default 1
  //   in_49: default 1
  //   in_66: default 1
  //   in_68: default 1
  //   contents of eeprom_1 (hex, n*v repeats v):
  //   54,61,7fff,11*ffff,11,22,240*ffff
  //   contents of eeprom_2 (hex, n*v repeats v):
  //   effd,27fe6,7fff,13*ffff,fff8,bbee,13fff,17fff,12*ffff,fff8,feee
  //   ,ffff,13fff,220*ffff
endmodule
