// Digital circuit Nor Gate half adder.dig as structural Verilog
module Nor_Gate_half_adder (
  input  a,
  input  b,
  output s,
  output c
);

  wire nor_1_out, nor_2_out, nor_4_out;

  nor nor_1 (nor_1_out, ~a, b);  // NOr
  nor nor_2 (nor_2_out, a, ~b);  // NOr
  nor nor_3 (c, ~b, ~a);  // NOr
  nor nor_4 (nor_4_out, nor_1_out, nor_2_out);
  nor nor_5 (s, nor_4_out, nor_4_out);
endmodule
