// Digital circuit Wazm8CPU.dig as structural Verilog
module Wazm8CPU (
  input  in_9,
  input  in_10,
  input  in_11,
  input  in_12,
  input  in_13,
  input  in_14,
  input  in_15,
  input  in_16,
  input  in_17,
  input  in_18,
  input  in_19,
  input  in_20,
  input  Auto_clock,
  input  Manual_clock,
  input  in_23,
  input  in_24,
  input  in_25,
  input  in_27,
  input  in_28,
  input  in_29,
  input  in_30,
  input  in_31,
  input  in_32,
  input  in_33,
  input  in_34,
  input  in_36,
  input  clk,
  input  in_38,
  input  Reg_A_Reset,
  input  Reg_TEMP_Reset,
  input  in_42,
  input  in_43,
  input  in_44,
  input  in_45,
  input  in_46,
  input  in_47,
  input  Reg_B_Reset,
  input  in_49,
  input  in_50,
  input  Reg_C_Reset,
  input  in_52,
  input  in_53,
  input  Reg_D_Reset,
  input  in_55,
  input  in_56,
  input  Reg_E_Reset,
  input  in_58,
  input  in_59,
  input  in_60,
  input  in_61,
  input  in_62,
  input  in_63,
  input  in_64,
  input  in_65,
  input  in_66,
  input  in_67,
  input  in_68,
  input  in_69,
  input  in_70,
  input  in_71,
  input  in_72,
  input  in_73,
  input  in_74,
  input  in_75,
  input  in_76,
  input  in_77,
  input  in_78,
  input  in_79,
  input  in_83,
  input  in_84,
  output out_1,
  output out_2,
  output out_3,
  output out_4,
  output out_5,
  output out_6,
  output out_7,
  output out_8,
  output out_26,
  output out_35,
  output out_41,
  output out_80,
  output out_81,
  output out_82
);

  wire _7483real_1_pin4, _7483real_1_pin7, _7483real_1_pin11, _7483real_1_pin14, _7483real_1_pin16,
       _7483real_2_pin4, _7483real_2_pin7, _7483real_2_pin11, _7483real_2_pin16, _7485_1_pin5, _7485_1_pin6,
       _7485_1_pin7, _74161_1_pin15, _74161_3_pin3, _74161_3_pin4, _74161_3_pin5, _74161_3_pin6,
       _74161_3_pin11, _74161_3_pin12, _74161_3_pin13, _74161_3_pin14, _74161_3_pin15, _74161_4_pin3,
       _74161_4_pin4, _74161_4_pin5, _74161_4_pin6, _74161_4_pin11, _74161_4_pin12, _74161_4_pin13,
       _74161_4_pin14, _74173_1_pin11, _74173_1_pin12, _74173_1_pin13, _74173_1_pin14, _74173_2_pin11,
       _74173_2_pin12, _74173_2_pin13, _74173_2_pin14, _74173_3_pin3, _74173_3_pin4, _74173_3_pin5,
       _74173_3_pin6, _74173_3_pin11, _74173_3_pin12, _74173_3_pin13, _74173_3_pin14, _74173_4_pin3,
       _74173_4_pin4, _74173_4_pin5, _74173_4_pin6, _74173_4_pin11, _74173_4_pin12, _74173_4_pin13,
       _74173_4_pin14, _74173_5_pin3, _74173_5_pin4, _74173_5_pin5, _74173_5_pin6, _74173_5_pin11,
       _74173_5_pin12, _74173_5_pin13, _74173_5_pin14, _74173_6_pin3, _74173_6_pin4, _74173_6_pin5,
       _74173_6_pin6, _74173_6_pin11, _74173_6_pin12, _74173_6_pin13, _74173_6_pin14, _74245_1_pin11,
       _74245_1_pin12, _74245_1_pin13, _74245_1_pin14, _74245_1_pin15, _74245_1_pin16, _74245_1_pin17,
       _74245_1_pin18, _74245_2_pin11, _74245_2_pin12, _74245_2_pin13, _74245_2_pin14, _74245_2_pin15,
       _74245_2_pin16, _74245_2_pin17, _74245_2_pin18, _74245_3_pin11, _74245_3_pin12, _74245_3_pin13,
       _74245_3_pin14, _74245_3_pin15, _74245_3_pin16, _74245_3_pin17, _74245_3_pin18, _74245_13_pin11,
       _74245_13_pin12, _74245_13_pin13, _74245_13_pin14, _74245_13_pin15, _74245_13_pin16, _74245_13_pin17,
       _74245_13_pin18, _74245_14_pin11, _74245_14_pin12, _74245_14_pin13, _74245_14_pin14, _74245_14_pin15,
       _74245_14_pin16, _74245_14_pin17, _74245_14_pin18, _74245_15_pin11, _74245_15_pin12, _74245_15_pin13,
       _74245_15_pin14, _74245_15_pin15, _74245_15_pin16, _74245_15_pin17, _74245_15_pin18, _74245_16_pin11,
       _74245_16_pin12, _74245_16_pin13, _74245_16_pin14, _74245_16_pin15, _74245_16_pin16, _74245_16_pin17,
       _74245_16_pin18, _74245_17_pin11, _74245_17_pin12, _74245_17_pin13, _74245_17_pin14, _74245_17_pin15,
       _74245_17_pin16, _74245_17_pin17, _74245_17_pin18, _74245_18_pin11, _74245_18_pin12, _74245_18_pin13,
       _74245_18_pin14, _74245_18_pin15, _74245_18_pin16, _74245_18_pin17, _74245_18_pin18, _74245_19_pin11,
       _74245_19_pin12, _74245_19_pin13, _74245_19_pin14, _74245_19_pin15, _74245_19_pin16, _74245_19_pin17,
       _74245_19_pin18, ALUOUT, and_1_out, and_2_out, and_3_out, and_4_out, CLOCK, COUNTIN, COUNTOUT, IRIN,
       IRIN2, IROUT, IROUT2, LDA, LDB, LDC, LDD, LDE, LDTEMP, MARIN, MAROUT, OE, OUTA, OUTB, OUTC, OUTD,
       OUTE, OUTTEMP, PROGRAMMER, RAMIN, RAMOUT, WE;
  wire [7:0] _74161_2_pin11, eeprom_1_d;

  not not_1 (PROGRAMMER, in_38);
  and and_1 (and_1_out, in_38, clk);
  not not_2 (RAMOUT, in_12);
  not not_3 (RAMIN, in_13);
  not not_4 (WE, in_14);
  not not_5 (OE, in_15);
  not not_6 (COUNTIN, in_23);
  not not_7 (COUNTOUT, in_24);
  not not_8 (IRIN, in_28);
  not not_9 (IROUT, in_29);
  not not_10 (IRIN2, in_83);
  not not_11 (IROUT2, in_84);
  not not_12 (MARIN, in_31);
  not not_13 (MAROUT, in_32);
  not not_14 (ALUOUT, in_78);
  not not_15 (OUTA, in_60);
  not not_16 (LDA, in_72);
  not not_17 (OUTTEMP, in_62);
  not not_18 (LDTEMP, in_73);
  not not_19 (OUTB, in_64);
  not not_20 (LDB, in_74);
  not not_21 (OUTC, in_66);
  not not_22 (LDC, in_75);
  not not_23 (OUTD, in_68);
  not not_24 (LDD, in_76);
  not not_25 (OUTE, in_70);
  not not_26 (LDE, in_77);
  _74161 _74161_1 (
    .pin1(in_34), .pin2(and_1_out), .pin3(1'b0), .pin4(1'b0), .pin5(1'b0), .pin6(1'b0), .pin7(in_38),
    .pin8(1'b0), .pin9(COUNTIN), .pin10(1'b1), .pin11(_74161_2_pin11[3]), .pin12(_74161_2_pin11[2]),
    .pin13(_74161_2_pin11[1]), .pin14(_74161_2_pin11[0]), .pin15(_74161_1_pin15), .pin16(1'b1));
  _74161 _74161_2 (
    .pin1(in_36), .pin2(and_1_out), .pin3(1'b0), .pin4(1'b0), .pin5(1'b0), .pin6(1'b0),
    .pin7(_74161_1_pin15), .pin8(1'b0), .pin9(COUNTIN), .pin10(1'b1), .pin11(_74161_2_pin11[7]),
    .pin12(_74161_2_pin11[6]), .pin13(_74161_2_pin11[5]), .pin14(_74161_2_pin11[4]), .pin15(out_35),
    .pin16(1'b1));
  and and_2 (and_2_out, Auto_clock, in_20);
  and and_3 (and_3_out, ~in_20, Manual_clock);  // And
  EEPROM #(.AddrBits(8), .Bits(8)) eeprom_1 (.A(_74161_2_pin11), .CS(in_11), .WE(in_10), .OE(in_9), .D(eeprom_1_d));
  or or_1 (CLOCK, and_2_out, and_3_out);
  _74245 _74245_1 (
    .pin1(1'b1), .pin2(eeprom_1_d[0]), .pin3(eeprom_1_d[1]), .pin4(eeprom_1_d[2]), .pin5(eeprom_1_d[3]),
    .pin6(eeprom_1_d[4]), .pin7(eeprom_1_d[5]), .pin8(eeprom_1_d[6]), .pin9(eeprom_1_d[7]), .pin10(1'b0),
    .pin11(_74245_1_pin11), .pin12(_74245_1_pin12), .pin13(_74245_1_pin13), .pin14(_74245_1_pin14),
    .pin15(_74245_1_pin15), .pin16(_74245_1_pin16), .pin17(_74245_1_pin17), .pin18(_74245_1_pin18),
    .pin19(PROGRAMMER), .pin20(1'b1));
  _74245 _74245_2 (
    .pin1(1'b1), .pin2(_74161_2_pin11[0]), .pin3(_74161_2_pin11[1]), .pin4(_74161_2_pin11[2]),
    .pin5(_74161_2_pin11[3]), .pin6(_74161_2_pin11[4]), .pin7(_74161_2_pin11[5]), .pin8(_74161_2_pin11[6]),
    .pin9(_74161_2_pin11[7]), .pin10(1'b0), .pin11(_74245_2_pin11), .pin12(_74245_2_pin12),
    .pin13(_74245_2_pin13), .pin14(_74245_2_pin14), .pin15(_74245_2_pin15), .pin16(_74245_2_pin16),
    .pin17(_74245_2_pin17), .pin18(_74245_2_pin18), .pin19(PROGRAMMER), .pin20(1'b1));
  _74245 _74245_3 (
    .pin1(1'b0), .pin2(_74245_2_pin18), .pin3(_74245_2_pin17), .pin4(_74245_2_pin16), .pin5(_74245_2_pin15),
    .pin6(_74245_2_pin14), .pin7(_74245_2_pin13), .pin8(_74245_2_pin12), .pin9(_74245_2_pin11), .pin10(1'b0),
    .pin11(_74245_3_pin11), .pin12(_74245_3_pin12), .pin13(_74245_3_pin13), .pin14(_74245_3_pin14),
    .pin15(_74245_3_pin15), .pin16(_74245_3_pin16), .pin17(_74245_3_pin17), .pin18(_74245_3_pin18),
    .pin19(MAROUT), .pin20(1'b1));
  // A623308A a623308a_1: pin names not known; wires that end beside it: 1'b0, _74245_2_pin11, _74245_2_pin12, _74245_2_pin13, _74245_2_pin14, _74245_2_pin15, _74245_2_pin16, _74245_2_pin17, _74245_2_pin18, _74245_1_pin18, _74245_1_pin17, _74245_1_pin16, 1'b0, 1'b1, WE, 1'b0, 1'b0, 1'b0, OE, 1'b0, in_16, _74245_1_pin11
  and and_4 (and_4_out, _74161_3_pin15, in_25);
  _74173 _74173_1 (
    .pin1(1'b0), .pin2(1'b0), .pin3(_74245_3_pin18), .pin4(_74245_3_pin17), .pin5(_74245_3_pin16),
    .pin6(_74245_3_pin15), .pin7(CLOCK), .pin8(1'b0), .pin9(MARIN), .pin10(MARIN), .pin11(_74173_1_pin11),
    .pin12(_74173_1_pin12), .pin13(_74173_1_pin13), .pin14(_74173_1_pin14), .pin15(in_33), .pin16(1'b1));
  _74173 _74173_2 (
    .pin1(1'b0), .pin2(1'b0), .pin3(_74245_3_pin14), .pin4(_74245_3_pin13), .pin5(_74245_3_pin12),
    .pin6(_74245_3_pin11), .pin7(CLOCK), .pin8(1'b0), .pin9(MARIN), .pin10(MARIN), .pin11(_74173_2_pin11),
    .pin12(_74173_2_pin12), .pin13(_74173_2_pin13), .pin14(_74173_2_pin14), .pin15(in_33), .pin16(1'b1));
  _74161 _74161_3 (
    .pin1(in_18), .pin2(CLOCK), .pin3(_74161_3_pin3), .pin4(_74161_3_pin4), .pin5(_74161_3_pin5),
    .pin6(_74161_3_pin6), .pin7(in_25), .pin8(1'b0), .pin9(COUNTIN), .pin10(1'b1), .pin11(_74161_3_pin11),
    .pin12(_74161_3_pin12), .pin13(_74161_3_pin13), .pin14(_74161_3_pin14), .pin15(_74161_3_pin15),
    .pin16(1'b1));
  _74161 _74161_4 (
    .pin1(in_27), .pin2(CLOCK), .pin3(_74161_4_pin3), .pin4(_74161_4_pin4), .pin5(_74161_4_pin5),
    .pin6(_74161_4_pin6), .pin7(and_4_out), .pin8(1'b0), .pin9(COUNTIN), .pin10(1'b1),
    .pin11(_74161_4_pin11), .pin12(_74161_4_pin12), .pin13(_74161_4_pin13), .pin14(_74161_4_pin14),
    .pin15(out_26), .pin16(1'b1));
  _74173 _74173_3 (
    .pin1(1'b0), .pin2(1'b0), .pin3(_74173_3_pin3), .pin4(_74173_3_pin4), .pin5(_74173_3_pin5),
    .pin6(_74173_3_pin6), .pin7(CLOCK), .pin8(1'b0), .pin9(IRIN), .pin10(IRIN), .pin11(_74173_3_pin11),
    .pin12(_74173_3_pin12), .pin13(_74173_3_pin13), .pin14(_74173_3_pin14), .pin15(in_30), .pin16(1'b1));
  _74173 _74173_4 (
    .pin1(1'b0), .pin2(1'b0), .pin3(_74173_4_pin3), .pin4(_74173_4_pin4), .pin5(_74173_4_pin5),
    .pin6(_74173_4_pin6), .pin7(CLOCK), .pin8(1'b0), .pin9(IRIN), .pin10(IRIN), .pin11(_74173_4_pin11),
    .pin12(_74173_4_pin12), .pin13(_74173_4_pin13), .pin14(_74173_4_pin14), .pin15(in_30), .pin16(1'b1));
  _74173 _74173_5 (
    .pin1(1'b0), .pin2(1'b0), .pin3(_74173_5_pin3), .pin4(_74173_5_pin4), .pin5(_74173_5_pin5),
    .pin6(_74173_5_pin6), .pin7(CLOCK), .pin8(1'b0), .pin9(IRIN2), .pin10(IRIN2), .pin11(_74173_5_pin11),
    .pin12(_74173_5_pin12), .pin13(_74173_5_pin13), .pin14(_74173_5_pin14), .pin15(in_30), .pin16(1'b1));
  _74173 _74173_6 (
    .pin1(1'b0), .pin2(1'b0), .pin3(_74173_6_pin3), .pin4(_74173_6_pin4), .pin5(_74173_6_pin5),
    .pin6(_74173_6_pin6), .pin7(CLOCK), .pin8(1'b0), .pin9(IRIN2), .pin10(IRIN2), .pin11(_74173_6_pin11),
    .pin12(_74173_6_pin12), .pin13(_74173_6_pin13), .pin14(_74173_6_pin14), .pin15(in_30), .pin16(1'b1));
  _74245 _74245_4 (
    .pin1(1'b0), .pin2(_74173_1_pin14), .pin3(_74173_1_pin13), .pin4(_74173_1_pin12), .pin5(_74173_1_pin11),
    .pin6(_74173_2_pin14), .pin7(_74173_2_pin13), .pin8(_74173_2_pin12), .pin9(_74173_2_pin11), .pin10(1'b0),
    .pin11(out_1), .pin12(out_2), .pin13(out_3), .pin14(out_4), .pin15(out_5), .pin16(out_6), .pin17(out_7),
    .pin18(out_8), .pin19(MARIN), .pin20(1'b1));
  _74245 _74245_5 (
    .pin1(1'b0), .pin2(_74245_1_pin18), .pin3(_74245_1_pin17), .pin4(_74245_1_pin16), .pin5(_74245_1_pin15),
    .pin6(_74245_1_pin14), .pin7(_74245_1_pin13), .pin8(_74245_1_pin12), .pin9(_74245_1_pin11), .pin10(1'b0),
    .pin11(out_1), .pin12(out_2), .pin13(out_3), .pin14(out_4), .pin15(out_5), .pin16(out_6), .pin17(out_7),
    .pin18(out_8), .pin19(RAMIN), .pin20(1'b1));
  _74245 _74245_6 (
    .pin1(1'b1), .pin2(_74245_1_pin18), .pin3(_74245_1_pin17), .pin4(_74245_1_pin16), .pin5(_74245_1_pin15),
    .pin6(_74245_1_pin14), .pin7(_74245_1_pin13), .pin8(_74245_1_pin12), .pin9(_74245_1_pin11), .pin10(1'b0),
    .pin11(out_1), .pin12(out_2), .pin13(out_3), .pin14(out_4), .pin15(out_5), .pin16(out_6), .pin17(out_7),
    .pin18(out_8), .pin19(RAMOUT), .pin20(1'b1));
  _74245 _74245_7 (
    .pin1(1'b0), .pin2(_74161_3_pin3), .pin3(_74161_3_pin4), .pin4(_74161_3_pin5), .pin5(_74161_3_pin6),
    .pin6(_74161_4_pin3), .pin7(_74161_4_pin4), .pin8(_74161_4_pin5), .pin9(_74161_4_pin6), .pin10(1'b0),
    .pin11(out_1), .pin12(out_2), .pin13(out_3), .pin14(out_4), .pin15(out_5), .pin16(out_6), .pin17(out_7),
    .pin18(out_8), .pin19(COUNTIN), .pin20(1'b1));
  _74245 _74245_8 (
    .pin1(1'b1), .pin2(_74161_3_pin14), .pin3(_74161_3_pin13), .pin4(_74161_3_pin12), .pin5(_74161_3_pin11),
    .pin6(_74161_4_pin14), .pin7(_74161_4_pin13), .pin8(_74161_4_pin12), .pin9(_74161_4_pin11), .pin10(1'b0),
    .pin11(out_1), .pin12(out_2), .pin13(out_3), .pin14(out_4), .pin15(out_5), .pin16(out_6), .pin17(out_7),
    .pin18(out_8), .pin19(COUNTOUT), .pin20(1'b1));
  _74245 _74245_9 (
    .pin1(1'b0), .pin2(_74173_3_pin14), .pin3(_74173_3_pin13), .pin4(_74173_3_pin12), .pin5(_74173_3_pin11),
    .pin6(_74173_4_pin14), .pin7(_74173_4_pin13), .pin8(_74173_4_pin12), .pin9(_74173_4_pin11), .pin10(1'b0),
    .pin11(out_1), .pin12(out_2), .pin13(out_3), .pin14(out_4), .pin15(out_5), .pin16(out_6), .pin17(out_7),
    .pin18(out_8), .pin19(IRIN), .pin20(1'b1));
  _74245 _74245_10 (
    .pin1(1'b1), .pin2(_74173_3_pin3), .pin3(_74173_3_pin4), .pin4(_74173_3_pin5), .pin5(_74173_3_pin6),
    .pin6(_74173_4_pin3), .pin7(_74173_4_pin4), .pin8(_74173_4_pin5), .pin9(_74173_4_pin6), .pin10(1'b0),
    .pin11(out_1), .pin12(out_2), .pin13(out_3), .pin14(out_4), .pin15(out_5), .pin16(out_6), .pin17(out_7),
    .pin18(out_8), .pin19(IROUT), .pin20(1'b1));
  _74245 _74245_11 (
    .pin1(1'b0), .pin2(_74173_5_pin14), .pin3(_74173_5_pin13), .pin4(_74173_5_pin12), .pin5(_74173_5_pin11),
    .pin6(_74173_6_pin14), .pin7(_74173_6_pin13), .pin8(_74173_6_pin12), .pin9(_74173_6_pin11), .pin10(1'b0),
    .pin11(out_1), .pin12(out_2), .pin13(out_3), .pin14(out_4), .pin15(out_5), .pin16(out_6), .pin17(out_7),
    .pin18(out_8), .pin19(IRIN2), .pin20(1'b1));
  _74245 _74245_12 (
    .pin1(1'b1), .pin2(_74173_5_pin3), .pin3(_74173_5_pin4), .pin4(_74173_5_pin5), .pin5(_74173_5_pin6),
    .pin6(_74173_6_pin3), .pin7(_74173_6_pin4), .pin8(_74173_6_pin5), .pin9(_74173_6_pin6), .pin10(1'b0),
    .pin11(out_1), .pin12(out_2), .pin13(out_3), .pin14(out_4), .pin15(out_5), .pin16(out_6), .pin17(out_7),
    .pin18(out_8), .pin19(IROUT2), .pin20(1'b1));
  _74245 _74245_13 (
    .pin1(1'b0), .pin2(out_8), .pin3(out_7), .pin4(out_6), .pin5(out_5), .pin6(out_4), .pin7(out_3),
    .pin8(out_2), .pin9(out_1), .pin10(1'b0), .pin11(_74245_13_pin11), .pin12(_74245_13_pin12),
    .pin13(_74245_13_pin13), .pin14(_74245_13_pin14), .pin15(_74245_13_pin15), .pin16(_74245_13_pin16),
    .pin17(_74245_13_pin17), .pin18(_74245_13_pin18), .pin19(ALUOUT), .pin20(1'b1));
  _74245 _74245_14 (
    .pin1(1'b0), .pin2(out_8), .pin3(out_7), .pin4(out_6), .pin5(out_5), .pin6(out_4), .pin7(out_3),
    .pin8(out_2), .pin9(out_1), .pin10(1'b0), .pin11(_74245_14_pin11), .pin12(_74245_14_pin12),
    .pin13(_74245_14_pin13), .pin14(_74245_14_pin14), .pin15(_74245_14_pin15), .pin16(_74245_14_pin16),
    .pin17(_74245_14_pin17), .pin18(_74245_14_pin18), .pin19(OUTB), .pin20(1'b1));
  _74245 _74245_15 (
    .pin1(1'b0), .pin2(out_8), .pin3(out_7), .pin4(out_6), .pin5(out_5), .pin6(out_4), .pin7(out_3),
    .pin8(out_2), .pin9(out_1), .pin10(1'b0), .pin11(_74245_15_pin11), .pin12(_74245_15_pin12),
    .pin13(_74245_15_pin13), .pin14(_74245_15_pin14), .pin15(_74245_15_pin15), .pin16(_74245_15_pin16),
    .pin17(_74245_15_pin17), .pin18(_74245_15_pin18), .pin19(OUTC), .pin20(1'b1));
  _74245 _74245_16 (
    .pin1(1'b0), .pin2(out_8), .pin3(out_7), .pin4(out_6), .pin5(out_5), .pin6(out_4), .pin7(out_3),
    .pin8(out_2), .pin9(out_1), .pin10(1'b0), .pin11(_74245_16_pin11), .pin12(_74245_16_pin12),
    .pin13(_74245_16_pin13), .pin14(_74245_16_pin14), .pin15(_74245_16_pin15), .pin16(_74245_16_pin16),
    .pin17(_74245_16_pin17), .pin18(_74245_16_pin18), .pin19(OUTD), .pin20(1'b1));
  _74245 _74245_17 (
    .pin1(1'b0), .pin2(out_8), .pin3(out_7), .pin4(out_6), .pin5(out_5), .pin6(out_4), .pin7(out_3),
    .pin8(out_2), .pin9(out_1), .pin10(1'b0), .pin11(_74245_17_pin11), .pin12(_74245_17_pin12),
    .pin13(_74245_17_pin13), .pin14(_74245_17_pin14), .pin15(_74245_17_pin15), .pin16(_74245_17_pin16),
    .pin17(_74245_17_pin17), .pin18(_74245_17_pin18), .pin19(OUTE), .pin20(1'b1));
  _74245 _74245_18 (
    .pin1(1'b0), .pin2(out_8), .pin3(out_7), .pin4(out_6), .pin5(out_5), .pin6(out_4), .pin7(out_3),
    .pin8(out_2), .pin9(out_1), .pin10(1'b0), .pin11(_74245_18_pin11), .pin12(_74245_18_pin12),
    .pin13(_74245_18_pin13), .pin14(_74245_18_pin14), .pin15(_74245_18_pin15), .pin16(_74245_18_pin16),
    .pin17(_74245_18_pin17), .pin18(_74245_18_pin18), .pin19(OUTA), .pin20(1'b1));
  _7483Real _7483real_1 (
    .pin1(_74245_18_pin15), .pin2(_74245_13_pin16), .pin3(_74245_18_pin16), .pin4(_7483real_1_pin4),
    .pin5(1'b1), .pin6(_74245_13_pin17), .pin7(_7483real_1_pin7), .pin8(_74245_18_pin17),
    .pin9(_74245_13_pin18), .pin10(_74245_18_pin18), .pin11(_7483real_1_pin11), .pin12(1'b0), .pin13(in_79),
    .pin14(_7483real_1_pin14), .pin15(_74245_13_pin15), .pin16(_7483real_1_pin16));
  _7483Real _7483real_2 (
    .pin1(_74245_18_pin11), .pin2(_74245_13_pin12), .pin3(_74245_18_pin12), .pin4(_7483real_2_pin4),
    .pin5(1'b1), .pin6(_74245_13_pin13), .pin7(_7483real_2_pin7), .pin8(_74245_18_pin13),
    .pin9(_74245_13_pin14), .pin10(_74245_18_pin14), .pin11(_7483real_2_pin11), .pin12(1'b0),
    .pin13(_7483real_1_pin14), .pin14(out_41), .pin15(_74245_13_pin11), .pin16(_7483real_2_pin16));
  _74245 _74245_19 (
    .pin1(1'b0), .pin2(out_8), .pin3(out_7), .pin4(out_6), .pin5(out_5), .pin6(out_4), .pin7(out_3),
    .pin8(out_2), .pin9(out_1), .pin10(1'b0), .pin11(_74245_19_pin11), .pin12(_74245_19_pin12),
    .pin13(_74245_19_pin13), .pin14(_74245_19_pin14), .pin15(_74245_19_pin15), .pin16(_74245_19_pin16),
    .pin17(_74245_19_pin17), .pin18(_74245_19_pin18), .pin19(OUTTEMP), .pin20(1'b1));
  _7486 _7486_1 (
    .pin1(_74245_19_pin18), .pin2(in_79), .pin3(_7483real_1_pin11), .pin4(_74245_19_pin17), .pin5(in_79),
    .pin6(_7483real_1_pin7), .pin7(1'b0), .pin8(_7483real_1_pin4), .pin9(_74245_19_pin16), .pin10(in_79),
    .pin11(_7483real_1_pin16), .pin12(_74245_19_pin15), .pin13(in_79), .pin14(1'b1));
  _7486 _7486_2 (
    .pin1(_74245_19_pin14), .pin2(in_79), .pin3(_7483real_2_pin11), .pin4(_74245_19_pin13), .pin5(in_79),
    .pin6(_7483real_2_pin7), .pin7(1'b0), .pin8(_7483real_2_pin4), .pin9(_74245_19_pin12), .pin10(in_79),
    .pin11(_7483real_2_pin16), .pin12(_74245_19_pin11), .pin13(in_79), .pin14(1'b1));
  _74173 _74173_7 (
    .pin1(1'b0), .pin2(1'b0), .pin3(_74245_14_pin18), .pin4(_74245_14_pin17), .pin5(_74245_14_pin16),
    .pin6(_74245_14_pin15), .pin7(CLOCK), .pin8(1'b0), .pin9(LDB), .pin10(LDB), .pin11(out_5), .pin12(out_6),
    .pin13(out_7), .pin14(out_8), .pin15(Reg_B_Reset), .pin16(1'b1));
  _74173 _74173_8 (
    .pin1(1'b0), .pin2(1'b0), .pin3(_74245_14_pin14), .pin4(_74245_14_pin13), .pin5(_74245_14_pin12),
    .pin6(_74245_14_pin11), .pin7(CLOCK), .pin8(1'b0), .pin9(LDB), .pin10(LDB), .pin11(out_1), .pin12(out_2),
    .pin13(out_3), .pin14(out_4), .pin15(Reg_B_Reset), .pin16(1'b1));
  _74173 _74173_9 (
    .pin1(1'b0), .pin2(1'b0), .pin3(_74245_15_pin18), .pin4(_74245_15_pin17), .pin5(_74245_15_pin16),
    .pin6(_74245_15_pin15), .pin7(CLOCK), .pin8(1'b0), .pin9(LDC), .pin10(LDC), .pin11(out_5), .pin12(out_6),
    .pin13(out_7), .pin14(out_8), .pin15(Reg_C_Reset), .pin16(1'b1));
  _74173 _74173_10 (
    .pin1(1'b0), .pin2(1'b0), .pin3(_74245_15_pin14), .pin4(_74245_15_pin13), .pin5(_74245_15_pin12),
    .pin6(_74245_15_pin11), .pin7(CLOCK), .pin8(1'b0), .pin9(LDC), .pin10(LDC), .pin11(out_1), .pin12(out_2),
    .pin13(out_3), .pin14(out_4), .pin15(Reg_C_Reset), .pin16(1'b1));
  _74173 _74173_11 (
    .pin1(1'b0), .pin2(1'b0), .pin3(_74245_16_pin18), .pin4(_74245_16_pin17), .pin5(_74245_16_pin16),
    .pin6(_74245_16_pin15), .pin7(CLOCK), .pin8(1'b0), .pin9(LDD), .pin10(LDD), .pin11(out_5), .pin12(out_6),
    .pin13(out_7), .pin14(out_8), .pin15(Reg_D_Reset), .pin16(1'b1));
  _74173 _74173_12 (
    .pin1(1'b0), .pin2(1'b0), .pin3(_74245_16_pin14), .pin4(_74245_16_pin13), .pin5(_74245_16_pin12),
    .pin6(_74245_16_pin11), .pin7(CLOCK), .pin8(1'b0), .pin9(LDD), .pin10(LDD), .pin11(out_1), .pin12(out_2),
    .pin13(out_3), .pin14(out_4), .pin15(Reg_D_Reset), .pin16(1'b1));
  _74173 _74173_13 (
    .pin1(1'b0), .pin2(1'b0), .pin3(_74245_17_pin18), .pin4(_74245_17_pin17), .pin5(_74245_17_pin16),
    .pin6(_74245_17_pin15), .pin7(CLOCK), .pin8(1'b0), .pin9(LDE), .pin10(LDE), .pin11(out_5), .pin12(out_6),
    .pin13(out_7), .pin14(out_8), .pin15(Reg_E_Reset), .pin16(1'b1));
  _74173 _74173_14 (
    .pin1(1'b0), .pin2(1'b0), .pin3(_74245_17_pin14), .pin4(_74245_17_pin13), .pin5(_74245_17_pin12),
    .pin6(_74245_17_pin11), .pin7(CLOCK), .pin8(1'b0), .pin9(LDE), .pin10(LDE), .pin11(out_1), .pin12(out_2),
    .pin13(out_3), .pin14(out_4), .pin15(Reg_E_Reset), .pin16(1'b1));
  _74173 _74173_15 (
    .pin1(1'b0), .pin2(1'b0), .pin3(_74245_18_pin18), .pin4(_74245_18_pin17), .pin5(_74245_18_pin16),
    .pin6(_74245_18_pin15), .pin7(CLOCK), .pin8(1'b0), .pin9(LDA), .pin10(LDA), .pin11(out_5), .pin12(out_6),
    .pin13(out_7), .pin14(out_8), .pin15(Reg_A_Reset), .pin16(1'b1));
  _74173 _74173_16 (
    .pin1(1'b0), .pin2(1'b0), .pin3(_74245_18_pin14), .pin4(_74245_18_pin13), .pin5(_74245_18_pin12),
    .pin6(_74245_18_pin11), .pin7(CLOCK), .pin8(1'b0), .pin9(LDA), .pin10(LDA), .pin11(out_1), .pin12(out_2),
    .pin13(out_3), .pin14(out_4), .pin15(Reg_A_Reset), .pin16(1'b1));
  _74173 _74173_17 (
    .pin1(1'b0), .pin2(1'b0), .pin3(_74245_19_pin18), .pin4(_74245_19_pin17), .pin5(_74245_19_pin16),
    .pin6(_74245_19_pin15), .pin7(CLOCK), .pin8(1'b0), .pin9(LDTEMP), .pin10(LDTEMP), .pin11(out_5),
    .pin12(out_6), .pin13(out_7), .pin14(out_8), .pin15(Reg_TEMP_Reset), .pin16(1'b1));
  _74173 _74173_18 (
    .pin1(1'b0), .pin2(1'b0), .pin3(_74245_19_pin14), .pin4(_74245_19_pin13), .pin5(_74245_19_pin12),
    .pin6(_74245_19_pin11), .pin7(CLOCK), .pin8(1'b0), .pin9(LDTEMP), .pin10(LDTEMP), .pin11(out_1),
    .pin12(out_2), .pin13(out_3), .pin14(out_4), .pin15(Reg_TEMP_Reset), .pin16(1'b1));
  _7485 _7485_1 (
    .pin1(_74245_19_pin15), .pin2(1'b0), .pin3(1'b0), .pin4(1'b0), .pin5(_7485_1_pin5), .pin6(_7485_1_pin6),
    .pin7(_7485_1_pin7), .pin8(1'b0), .pin9(_74245_19_pin18), .pin10(_74245_18_pin18),
    .pin11(_74245_19_pin17), .pin12(_74245_18_pin17), .pin13(_74245_18_pin16), .pin14(_74245_19_pin16),
    .pin15(_74245_18_pin15), .pin16(1'b1));
  _7485 _7485_2 (
    .pin1(_74245_19_pin11), .pin2(_7485_1_pin7), .pin3(_7485_1_pin6), .pin4(_7485_1_pin5), .pin5(out_80),
    .pin6(out_81), .pin7(out_82), .pin8(1'b0), .pin9(_74245_19_pin14), .pin10(_74245_18_pin14),
    .pin11(_74245_19_pin13), .pin12(_74245_18_pin13), .pin13(_74245_18_pin12), .pin14(_74245_19_pin12),
    .pin15(_74245_18_pin11), .pin16(1'b1));

  // Other names for the same wires on the sheet: CE = in_16; COMPEQ = out_81; COMPGT = out_80; COMPLT = out_82;
  //   COUNTENABLE = in_25; IRRESET = in_30; MARRESET = in_33; Reg_A_Reset_t = in_61; Reg_B_Reset_t = in_65;
  //   Reg_C_Reset_t = in_67; Reg_D_Reset_t = in_69; Reg_E_Reset_t = in_71; Reg_TEMP_Reset_t = in_63; SUB = in_79

  // Notes on the sheet:
  //   in_9: default 1
  //   in_11: default 1
  //   in_17: default 1
  //   in_18: default 1
  //   in_19: default 1
  //   Auto_clock: Hz: 5
  //   in_27: default 1
  //   in_34: default 1
  //   in_36: default 1
  //   clk: Hz: 20
  //   PROGRAMMER
  //   contents of eeprom_1 (hex, n*v repeats v):
  //   3,1,2,11*ffff,11,22,240*ffff
  //   RAM OUT
  //   RAM IN
endmodule
