// Digital circuit jk with d 2.dig as structural Verilog
module jk_with_d_2 (
  input  clk,
  input  in_4,
  input  in_5,
  output out_2,
  output out_3
);

  wire and_1_out, and_2_out, or_1_out;

  and and_1 (and_1_out, out_3, in_4);
  and and_2 (and_2_out, ~in_5, out_2);  // And
  or or_1 (or_1_out, and_1_out, and_2_out);
  D_FF d_ff_1 (.D(or_1_out), .C(clk), .Q(out_2), .nQ(out_3));
endmodule
