// Digital circuit ripple coundet.dig as structural Verilog
module ripple_coundet (
  input  in_1,
  input  clk
);

  wire jk_ff_1_q, jk_ff_2_q, jk_ff_3_q, jk_ff_4_q;

  JK_FF jk_ff_1 (.J(in_1), .C(clk), .K(in_1), .Q(jk_ff_1_q));  // open: nQ
  JK_FF jk_ff_2 (.J(in_1), .C(jk_ff_1_q), .K(in_1), .Q(jk_ff_2_q));  // open: nQ
  LED led_1 (.in(jk_ff_1_q));
  LED led_2 (.in(jk_ff_2_q));
  JK_FF jk_ff_3 (.J(in_1), .C(jk_ff_2_q), .K(in_1), .Q(jk_ff_3_q));  // open: nQ
  JK_FF jk_ff_4 (.J(in_1), .C(jk_ff_3_q), .K(in_1), .Q(jk_ff_4_q));  // open: nQ
  LED led_3 (.in(jk_ff_3_q));
  LED led_4 (.in(jk_ff_4_q));

  // Notes on the sheet:
  //   in_1: default 1
  //   clk: Hz: 2
endmodule
